// Logisim project Lab_4.circ as structural Verilog: 9 circuits, main circuit One_Bit_Adder
module One_Bit_Adder (
  input  A,
  input  B,
  input  C_In,
  output S,
  output C_Out
);

  wire and_1_out, and_2_out, xor_1_out;

  xor xor_1 (xor_1_out, A, B);
  and and_1 (and_1_out, xor_1_out, C_In);
  and and_2 (and_2_out, A, B);
  xor xor_2 (S, xor_1_out, C_In);
  or or_1 (C_Out, and_1_out, and_2_out);
endmodule

module One_Bit_ALU (
  input  [3:0] ALU_Ctrl,
  input  A,
  input  B,
  input  C_In,
  output R,
  output C_Out
);

  wire and_1_out, multiplexer_1_out, not_1_out, one_bit_adder_1_s, or_1_out, xor_1_out;

  Multiplexer #(.enable("false")) multiplexer_1 (.in0(B), .in1(not_1_out), .out(multiplexer_1_out), .sel(ALU_Ctrl[2]));
  not not_1 (not_1_out, B);
  and and_1 (and_1_out, A, multiplexer_1_out);
  or or_1 (or_1_out, A, multiplexer_1_out);
  xor xor_1 (xor_1_out, A, multiplexer_1_out);
  Multiplexer #(.enable("false"), .select(2)) multiplexer_2 (
    .in0(and_1_out), .in1(or_1_out), .in2(xor_1_out), .in3(one_bit_adder_1_s), .out(R), .sel(ALU_Ctrl[1:0]));
  One_Bit_Adder one_bit_adder_1 (.A(A), .B(multiplexer_1_out), .C_In(C_In), .S(one_bit_adder_1_s), .C_Out(C_Out));
endmodule

module Four_Bit_ALU (
  input  [3:0] ALU_Ctrl,
  input  C_In,
  input  [3:0] A,
  input  [3:0] B,
  output [3:0] R,
  output C_Out
);

  wire one_bit_alu_1_c_out, one_bit_alu_2_c_out, one_bit_alu_3_c_out;

  One_Bit_ALU one_bit_alu_1 (
    .ALU_Ctrl(ALU_Ctrl), .A(A[0]), .B(B[0]), .C_In(C_In), .R(R[0]), .C_Out(one_bit_alu_1_c_out));
  One_Bit_ALU one_bit_alu_2 (
    .ALU_Ctrl(ALU_Ctrl), .A(A[1]), .B(B[1]), .C_In(one_bit_alu_1_c_out), .R(R[1]), .C_Out(one_bit_alu_2_c_out));
  One_Bit_ALU one_bit_alu_3 (
    .ALU_Ctrl(ALU_Ctrl), .A(A[2]), .B(B[2]), .C_In(one_bit_alu_2_c_out), .R(R[2]), .C_Out(one_bit_alu_3_c_out));
  One_Bit_ALU one_bit_alu_4 (
    .ALU_Ctrl(ALU_Ctrl), .A(A[3]), .B(B[3]), .C_In(one_bit_alu_3_c_out), .R(R[3]), .C_Out(C_Out));
endmodule

module Sixteen_Bit_ALU (
  input  [3:0] ALU_Ctrl,
  input  C_In,
  input  [15:0] A,
  input  [15:0] B,
  output [15:0] R,
  output C_Out
);

  wire four_bit_alu_1_c_out, four_bit_alu_2_c_out, four_bit_alu_3_c_out;

  Four_Bit_ALU four_bit_alu_1 (
    .ALU_Ctrl(ALU_Ctrl), .C_In(C_In), .A(A[3:0]), .B(B[3:0]), .R(R[3:0]), .C_Out(four_bit_alu_1_c_out));
  Four_Bit_ALU four_bit_alu_2 (
    .ALU_Ctrl(ALU_Ctrl), .C_In(four_bit_alu_1_c_out), .A(A[7:4]), .B(B[7:4]), .R(R[7:4]),
    .C_Out(four_bit_alu_2_c_out));
  Four_Bit_ALU four_bit_alu_3 (
    .ALU_Ctrl(ALU_Ctrl), .C_In(four_bit_alu_2_c_out), .A(A[11:8]), .B(B[11:8]), .R(R[11:8]),
    .C_Out(four_bit_alu_3_c_out));
  Four_Bit_ALU four_bit_alu_4 (
    .ALU_Ctrl(ALU_Ctrl), .C_In(four_bit_alu_3_c_out), .A(A[15:12]), .B(B[15:12]), .R(R[15:12]), .C_Out(C_Out));
endmodule

module ThirtyTwo_Bit_ALU (
  input  [3:0] ALU_Ctrl,
  input  C_In,
  input  [31:0] A,
  input  [31:0] B,
  output [31:0] R,
  output C_Out
);

  wire sixteen_bit_alu_1_c_out;

  Sixteen_Bit_ALU sixteen_bit_alu_1 (
    .ALU_Ctrl(ALU_Ctrl), .C_In(C_In), .A(A[15:0]), .B(B[15:0]), .R(R[15:0]), .C_Out(sixteen_bit_alu_1_c_out));
  Sixteen_Bit_ALU sixteen_bit_alu_2 (
    .ALU_Ctrl(ALU_Ctrl), .C_In(sixteen_bit_alu_1_c_out), .A(A[31:16]), .B(B[31:16]), .R(R[31:16]),
    .C_Out(C_Out));
endmodule

module Register_File (
  input  [4:0] RReg1,
  input  [31:0] WData,
  input  Clock_In,
  input  [4:0] Wreg,
  input  Write,
  input  [4:0] RReg2,
  output [31:0] RData1,
  output [31:0] RData2
);

  wire WriteEnable0, WriteEnable1, WriteEnable2, WriteEnable3, WriteEnable4, WriteEnable5, WriteEnable6,
       WriteEnable7, WriteEnable8, WriteEnable9, WriteEnable10, WriteEnable11, WriteEnable12, WriteEnable13,
       WriteEnable14, WriteEnable15, WriteEnable16, WriteEnable17, WriteEnable18, WriteEnable19,
       WriteEnable20, WriteEnable21, WriteEnable22, WriteEnable23, WriteEnable24, WriteEnable25,
       WriteEnable26, WriteEnable27, WriteEnable28, WriteEnable29, WriteEnable30, WriteEnable31;
  wire [31:0] Out0, Out1, Out2, Out3, Out4, Out5, Out6, Out7, Out8, Out9, Out10, Out11, Out12, Out13, Out14,
       Out15, Out16, Out17, Out18, Out19, Out20, Out21, Out22, Out23, Out24, Out25, Out26, Out27, Out28,
       Out29, Out30, Out31;

  Demultiplexer #(.enable("false"), .select(5)) demultiplexer_1 (
    .out0(WriteEnable0), .out1(WriteEnable1), .out2(WriteEnable2), .out3(WriteEnable3), .out4(WriteEnable4),
    .out5(WriteEnable5), .out6(WriteEnable6), .out7(WriteEnable7), .out8(WriteEnable8), .out9(WriteEnable9),
    .out10(WriteEnable10), .out11(WriteEnable11), .out12(WriteEnable12), .out13(WriteEnable13),
    .out14(WriteEnable14), .out15(WriteEnable15), .out16(WriteEnable16), .out17(WriteEnable17),
    .out18(WriteEnable18), .out19(WriteEnable19), .out20(WriteEnable20), .out21(WriteEnable21),
    .out22(WriteEnable22), .out23(WriteEnable23), .out24(WriteEnable24), .out25(WriteEnable25),
    .out26(WriteEnable26), .out27(WriteEnable27), .out28(WriteEnable28), .out29(WriteEnable29),
    .out30(WriteEnable30), .out31(WriteEnable31), .in(Write), .sel(Wreg));
  Register #(.width(32)) register_1 (.D(WData), .en(WriteEnable0), .clk(Clock_In), .Q(Out0), .clr(Write));
  Register #(.width(32)) register_2 (.D(WData), .en(WriteEnable1), .clk(Clock_In), .Q(Out1));  // open: clr
  Register #(.width(32)) register_3 (.D(WData), .en(WriteEnable2), .clk(Clock_In), .Q(Out2));  // open: clr
  Register #(.width(32)) register_4 (.D(WData), .en(WriteEnable3), .clk(Clock_In), .Q(Out3));  // open: clr
  Register #(.width(32)) register_5 (.D(WData), .en(WriteEnable4), .clk(Clock_In), .Q(Out4));  // open: clr
  Register #(.width(32)) register_6 (.D(WData), .en(WriteEnable5), .clk(Clock_In), .Q(Out5));  // open: clr
  Register #(.width(32)) register_7 (.D(WData), .en(WriteEnable6), .clk(Clock_In), .Q(Out6));  // open: clr
  Register #(.width(32)) register_8 (.D(WData), .en(WriteEnable7), .clk(Clock_In), .Q(Out7));  // open: clr
  Register #(.width(32)) register_9 (.D(WData), .en(WriteEnable8), .clk(Clock_In), .Q(Out8));  // open: clr
  Register #(.width(32)) register_10 (.D(WData), .en(WriteEnable9), .clk(Clock_In), .Q(Out9));  // open: clr
  Register #(.width(32)) register_11 (.D(WData), .en(WriteEnable10), .clk(Clock_In), .Q(Out10));  // open: clr
  Register #(.width(32)) register_12 (.D(WData), .en(WriteEnable11), .clk(Clock_In), .Q(Out11));  // open: clr
  Register #(.width(32)) register_13 (.D(WData), .en(WriteEnable12), .clk(Clock_In), .Q(Out12));  // open: clr
  Register #(.width(32)) register_14 (.D(WData), .en(WriteEnable13), .clk(Clock_In), .Q(Out13));  // open: clr
  Register #(.width(32)) register_15 (.D(WData), .en(WriteEnable14), .clk(Clock_In), .Q(Out14));  // open: clr
  Register #(.width(32)) register_16 (.D(WData), .en(WriteEnable15), .clk(Clock_In), .Q(Out15));  // open: clr
  Register #(.width(32)) register_17 (.D(WData), .en(WriteEnable16), .clk(Clock_In), .Q(Out16));  // open: clr
  Register #(.width(32)) register_18 (.D(WData), .en(WriteEnable17), .clk(Clock_In), .Q(Out17));  // open: clr
  Register #(.width(32)) register_19 (.D(WData), .en(WriteEnable18), .clk(Clock_In), .Q(Out18));  // open: clr
  Register #(.width(32)) register_20 (.D(WData), .en(WriteEnable19), .clk(Clock_In), .Q(Out19));  // open: clr
  Register #(.width(32)) register_21 (.D(WData), .en(WriteEnable20), .clk(Clock_In), .Q(Out20));  // open: clr
  Register #(.width(32)) register_22 (.D(WData), .en(WriteEnable21), .clk(Clock_In), .Q(Out21));  // open: clr
  Register #(.width(32)) register_23 (.D(WData), .en(WriteEnable22), .clk(Clock_In), .Q(Out22));  // open: clr
  Register #(.width(32)) register_24 (.D(WData), .en(WriteEnable23), .clk(Clock_In), .Q(Out23));  // open: clr
  Register #(.width(32)) register_25 (.D(WData), .en(WriteEnable24), .clk(Clock_In), .Q(Out24));  // open: clr
  Register #(.width(32)) register_26 (.D(WData), .en(WriteEnable25), .clk(Clock_In), .Q(Out25));  // open: clr
  Register #(.width(32)) register_27 (.D(WData), .en(WriteEnable26), .clk(Clock_In), .Q(Out26));  // open: clr
  Register #(.width(32)) register_28 (.D(WData), .en(WriteEnable27), .clk(Clock_In), .Q(Out27));  // open: clr
  Register #(.width(32)) register_29 (.D(WData), .en(WriteEnable28), .clk(Clock_In), .Q(Out28));  // open: clr
  Register #(.width(32)) register_30 (.D(WData), .en(WriteEnable29), .clk(Clock_In), .Q(Out29));  // open: clr
  Register #(.width(32)) register_31 (.D(WData), .en(WriteEnable30), .clk(Clock_In), .Q(Out30));  // open: clr
  Register #(.width(32)) register_32 (.D(WData), .en(WriteEnable31), .clk(Clock_In), .Q(Out31));  // open: clr
  Multiplexer #(.enable("false"), .select(5), .width(32)) multiplexer_1 (
    .in0(Out0), .in1(Out1), .in2(Out2), .in3(Out3), .in4(Out4), .in5(Out5), .in6(Out6), .in7(Out7),
    .in8(Out8), .in9(Out9), .in10(Out10), .in11(Out11), .in12(Out12), .in13(Out13), .in14(Out14),
    .in15(Out15), .in16(Out16), .in17(Out17), .in18(Out18), .in19(Out19), .in20(Out20), .in21(Out21),
    .in22(Out22), .in23(Out23), .in24(Out24), .in25(Out25), .in26(Out26), .in27(Out27), .in28(Out28),
    .in29(Out29), .in30(Out30), .in31(Out31), .out(RData1), .sel(RReg1));
  Multiplexer #(.enable("false"), .select(5), .width(32)) multiplexer_2 (
    .in0(Out0), .in1(Out1), .in2(Out2), .in3(Out3), .in4(Out4), .in5(Out5), .in6(Out6), .in7(Out7),
    .in8(Out8), .in9(Out9), .in10(Out10), .in11(Out11), .in12(Out12), .in13(Out13), .in14(Out14),
    .in15(Out15), .in16(Out16), .in17(Out17), .in18(Out18), .in19(Out19), .in20(Out20), .in21(Out21),
    .in22(Out22), .in23(Out23), .in24(Out24), .in25(Out25), .in26(Out26), .in27(Out27), .in28(Out28),
    .in29(Out29), .in30(Out30), .in31(Out31), .out(RData2), .sel(RReg2));

  // Other names for the same wires on the sheet: Clock = Clock_In; WriteData[31:0] = WData
endmodule

module ALU_Control (
  input  I30,
  input  I14,
  input  I13,
  input  I12,
  input  I6,
  input  I5,
  input  I4,
  output [3:0] ALU_Ctrl,
  output ALU_Src
);

  wire and_2_out, not_1_out, not_2_out, not_3_out, not_4_out, not_5_out;

  not not_1 (not_1_out, I14);
  not not_2 (not_2_out, I13);
  not not_3 (not_3_out, I12);
  not not_4 (not_4_out, I5);
  not not_5 (not_5_out, I4);
  and and_1 (ALU_Ctrl[2], I30, not_2_out, I5);
  or or_1 (ALU_Ctrl[1], not_2_out, not_5_out);
  and and_2 (and_2_out, I13, not_3_out);
  or or_2 (ALU_Src, not_4_out, not_5_out);
  or or_3 (ALU_Ctrl[0], not_1_out, and_2_out);

  assign ALU_Ctrl[3] = 1'b0;
endmodule

module Datapath (
  input  [31:0] Instruction
);

  wire alu_control_1_alu_src, clock_1_out;
  wire [3:0] alu_control_1_alu_ctrl;
  wire [31:0] bit_extender_1_out, multiplexer_1_out, register_file_1_rdata1, register_file_1_rdata2,
       thirtytwo_bit_alu_1_r;

  Clock clock_1 (.out(clock_1_out));
  assign bit_extender_1_out = {{20{Instruction[31]}}, Instruction[31:20]};  // Bit_Extender bit_extender_1
  Register_File register_file_1 (
    .RData1(register_file_1_rdata1), .RData2(register_file_1_rdata2), .WData(thirtytwo_bit_alu_1_r),
    .Clock_In(clock_1_out), .Wreg(Instruction[11:7]), .Write(1'b1), .RReg1(Instruction[19:15]),
    .RReg2(Instruction[24:20]));
  ALU_Control alu_control_1 (
    .I30(Instruction[30]), .I14(Instruction[14]), .I13(Instruction[13]), .I12(Instruction[12]),
    .I6(Instruction[6]), .I5(Instruction[5]), .I4(Instruction[4]), .ALU_Ctrl(alu_control_1_alu_ctrl),
    .ALU_Src(alu_control_1_alu_src));
  Multiplexer #(.enable("false"), .width(32)) multiplexer_1 (
    .in0(register_file_1_rdata2), .in1(bit_extender_1_out), .out(multiplexer_1_out),
    .sel(alu_control_1_alu_src));
  ThirtyTwo_Bit_ALU thirtytwo_bit_alu_1 (
    .ALU_Ctrl(alu_control_1_alu_ctrl), .A(register_file_1_rdata1), .B(multiplexer_1_out),
    .R(thirtytwo_bit_alu_1_r));  // open: C_In, C_Out
endmodule

module ImmGen (
  input  [31:0] Instruction,
  output [31:0] Imm32
);

  Multiplexer #(.enable("false")) multiplexer_1 (
    .in0(Instruction[31]), .in1(Instruction[7]), .out(Imm32[11]), .sel(Instruction[6]));
  Multiplexer #(.enable("false"), .width(4)) multiplexer_2 (
    .in0(Instruction[24:21]), .in1(Instruction[11:8]), .out(Imm32[4:1]), .sel(Instruction[5]));
  Multiplexer #(.enable("false"), .select(2)) multiplexer_3 (
    .in0(Instruction[20]), .in1(Instruction[7]), .in3(1'b0), .out(Imm32[0]), .sel(Instruction[6:5]));  // open: in2
  assign Imm32[31:12] = {{19{Instruction[31]}}, Instruction[31]};  // Bit_Extender bit_extender_1

  assign Imm32[10:5] = Instruction[30:25];

  // Other names for the same wires on the sheet: I30_25[5:0] = Instruction[30:25]; I5 = Instruction[5];
  //   I6_5[1:0] = Instruction[6:5]; I6 = Instruction[6]; I7 = Instruction[7]; I11_8[3:0] = Instruction[11:8];
  //   I20 = Instruction[20]; I24_21[3:0] = Instruction[24:21]; I31 = Instruction[31]
endmodule
